# Fritzing sketch ADXL335 (saved by Fritzing 0.8.7b)
breadboards: 1

parts:
  元件1 = Arduino Uno (Rev3)
  元件3 = Triple Axis Accelerometer Breakout - ADXL335

nets:
  N1: 元件1.A1, 元件3.XOUT
  N2: 元件1.A2, 元件3.YOUT
  N3: 元件1.A3, 元件3.ZOUT
  3V3: 元件1.3V3, 元件3.VCC
  GND: 元件1.GND, 元件3.GND
