# Fritzing sketch Simple Creation - Digital Dice (saved by Fritzing 0.8.7b)
breadboards: 1

parts:
  元件1 = Arduino Uno (Rev3)
  R1 = Resistor [tolerance=±5% resistance=220 package=THT]
  R2 = Resistor [tolerance=±5% resistance=220 package=THT]
  R3 = Resistor [tolerance=±5% resistance=220 package=THT]
  R4 = Resistor [tolerance=±5% resistance=220 package=THT]
  R5 = Resistor [tolerance=±5% resistance=220 package=THT]
  R6 = Resistor [tolerance=±5% resistance=220 package=THT]
  R7 = Resistor [tolerance=±5% resistance=220 package=THT]
  U1 = 74HC595 [package="DIP16 [THT]"]
  DI1 = 7-Segment LED Display [package=THT]
  R8 = Resistor [tolerance=±5% resistance=220 package=THT]
  S1 = Pushbutton [package="[THT]"]
  R9 = Resistor [tolerance=±5% resistance=220 package=THT]
  C1 = Ceramic Capacitor [capacitance=100nF package="100 mil [THT, multilayer]"]

nets (from the schematic view):
  N1: 元件1.D8, U1.SH_CP
  N2: 元件1.D11_PWM/MOSI, U1.DS
  N3: 元件1.D12/MISO, U1.ST_CP
  N4: 元件1.GND, U1.OE
  N5: 元件1.D2, S1.Pin_1, S1.Pin_2, R9.Pin_0, C1.1
  5V: 元件1.5V, U1.MR, U1.VCC
  N6: R1.Pin_0, U1.Q1
  N7: R1.Pin_1, DI1.cathodeG
  N8: R2.Pin_0, U1.Q3
  N9: R2.Pin_1, DI1.cathodeD
  N10: R3.Pin_0, DI1.cathodeC
  N11: R3.Pin_1, U1.Q5
  N12: R4.Pin_0, U1.Q2
  N13: R4.Pin_1, DI1.cathodeF
  N14: R5.Pin_0, DI1.cathodeDP
  N15: R5.Pin_1, U1.Q0
  N16: R6.Pin_0, DI1.cathodeA
  N17: R6.Pin_1, U1.Q7
  N18: R7.Pin_0, U1.Q4
  N19: R7.Pin_1, DI1.cathodeE
  N20: U1.Q6, R8.Pin_1
  N21: U1.GND, DI1.commAnode#2, R9.Pin_1, C1.0
  N22: DI1.cathodeB, R8.Pin_0
  N23: S1.Pin_3, S1.Pin_4
