# Fritzing sketch Controlling LED by Potentiometer (saved by Fritzing 0.8.7b)
breadboards: 1

parts:
  元件1 = Arduino Uno (Rev3)
  R1 = Resistor [tolerance=±5% resistance=220 package=THT]
  LED_RED = LED - 5mm [color="Red (633nm)" package="5 mm [THT]"]
  R2 = Rotary Potentiometer (Small) [maximum_resistance=100kΩ package=THT]

nets:
  N1: 元件1.A0, R2.wiper
  N2: 元件1.D9_PWM, R1.Pin_1
  N3: 元件1.GND, LED_RED.cathode, R2.leg1
  N4: 元件1.5V, R2.leg2
  N5: R1.Pin_0, LED_RED.anode
