# Fritzing sketch LED Flowing Lights (saved by Fritzing 0.8.7b)
breadboards: 1

parts:
  元件1 = Arduino Uno (Rev3)
  R1 = Resistor [tolerance=±5% resistance=220 package=THT]
  R2 = Resistor [tolerance=±5% resistance=220 package=THT]
  R3 = Resistor [tolerance=±5% resistance=220 package=THT]
  R4 = Resistor [tolerance=±5% resistance=220 package=THT]
  R5 = Resistor [tolerance=±5% resistance=220 package=THT]
  R6 = Resistor [tolerance=±5% resistance=220 package=THT]
  LED1 = LED - 5mm [color="Red (633nm)" package="5 mm [THT]"]
  LED2 = LED - 5mm [color="Green (570nm)" package="5 mm [THT]"]
  LED3 = LED - 5mm [color="Yellow (595nm)" package="5 mm [THT]"]
  LED4 = LED - 5mm [color="Red (633nm)" package="5 mm [THT]"]
  LED5 = LED - 5mm [color="Green (570nm)" package="5 mm [THT]"]
  LED6 = LED - 5mm [color="Yellow (595nm)" package="5 mm [THT]"]
  LED7 = LED - 5mm [color="Red (633nm)" package="5 mm [THT]"]
  LED8 = LED - 5mm [color="Red (633nm)" package="5 mm [THT]"]
  R7 = Resistor [tolerance=±5% resistance=220 package=THT]
  R8 = Resistor [tolerance=±5% resistance=220 package=THT]

nets:
  N1: 元件1.D8, R7.Pin_0
  N2: 元件1.D9_PWM, R8.Pin_0
  N3: 元件1.GND, LED1.cathode, LED2.cathode, LED3.cathode, LED4.cathode, LED5.cathode, LED6.cathode, LED7.cathode, LED8.cathode
  N4: 元件1.D2, R1.Pin_1
  N5: 元件1.D3_PWM, R2.Pin_0
  N6: 元件1.D4, R3.Pin_0
  N7: 元件1.D5_PWM, R4.Pin_0
  N8: 元件1.D6_PWM, R6.Pin_0
  N9: 元件1.D7, R5.Pin_0
  N10: R1.Pin_0, LED1.anode
  N11: R2.Pin_1, LED2.anode
  N12: R3.Pin_1, LED3.anode
  N13: R4.Pin_1, LED4.anode
  N14: R5.Pin_1, LED6.anode
  N15: R6.Pin_1, LED5.anode
  N16: LED7.anode, R7.Pin_1
  N17: LED8.anode, R8.Pin_1
