# Fritzing sketch RGB LED (saved by Fritzing 0.8.7b)
breadboards: 1

parts:
  元件1 = Arduino Uno (Rev3)
  RGB = RGB LED (com. anode, rbg) [package="5 mm [THT]"]
  R1 = Resistor [tolerance=±5% resistance=220 package=THT]
  R2 = Resistor [tolerance=±5% resistance=220 package=THT]
  R3 = Resistor [tolerance=±5% resistance=220 package=THT]

nets:
  N1: 元件1.D9_PWM, R2.Pin_0
  N2: 元件1.D10_PWM/SS, R3.Pin_0
  N3: 元件1.D11_PWM/MOSI, R1.Pin_0
  N4: 元件1.GND, RGB.common_anode
  N5: RGB.red_cathode, R1.Pin_1
  N6: RGB.blue_cathode, R3.Pin_1
  N7: RGB.green_cathode, R2.Pin_1
