# Fritzing sketch Rotary Encoder (saved by Fritzing 0.8.7b)
breadboards: 1

parts:
  元件1 = Arduino Uno (Rev3)
  R1 = Resistor [tolerance=±5% resistance=220 package=THT]
  C1 = Ceramic Capacitor [capacitance=100nF package="100 mil [THT, multilayer]"]
  R3 = Resistor [tolerance=±5% resistance=220 package=THT]
  C2 = Ceramic Capacitor [capacitance=100nF package="100 mil [THT, multilayer]"]
  RE1 = Rotary Encoder [package=THT]

nets:
  N1: 元件1.GND, C1.1, C2.0, RE1.EncoderPinC
  N2: 元件1.D2, R1.Pin_0, C1.0, RE1.EncoderPinB
  N3: 元件1.D3_PWM, R3.Pin_1, C2.1, RE1.EncoderPinA
  N4: 元件1.5V, R1.Pin_1, R3.Pin_0
