# Fritzing sketch Simple Creation - Light Alarm (saved by Fritzing 0.8.7b)
breadboards: 1

parts:
  元件1 = Arduino Uno (Rev3)
  buzzer = Piezo Speaker
  LED1 = LED - 5mm [color="Red (633nm)" package="5 mm [THT]"]
  Q1 = NPN-Transistor [package="TO92 [THT]"]
  R1 = Resistor [tolerance=±5% resistance=10k package=THT]

nets:
  N1: 元件1.A0, Q1.C, R1.Pin_0
  N2: 元件1.D4, buzzer.pin2
  N3: 元件1.5V, Q1.E
  N4: 元件1.GND, buzzer.pin1, LED1.cathode, R1.Pin_1
  N5: LED1.anode, Q1.B
