# Fritzing sketch 19. Simple Creation - Small Fan (saved by Fritzing 0.8.7b)
circuit board: 8.46667cm x 5.64444cm
breadboards: 1

parts:
  IC1 = L293D [package=THT]
  M1 = DC Motor
  D1 = Rectifier Diode [part_number=1N4001 package="300 mil [THT]"]
  D2 = Rectifier Diode [part_number=1N4001 package="300 mil [THT]"]
  D3 = Rectifier Diode [part_number=1N4001 package="300 mil [THT]"]
  D4 = Rectifier Diode [part_number=1N4001 package="300 mil [THT]"]
  U1 = Optocoupler [package=THT]
  U2 = Optocoupler [package=THT]
  R1 = Resistor [tolerance=±5% resistance=220 package=THT]
  R2 = Resistor [tolerance=±5% resistance=220 package=THT]
  R3 = Resistor [tolerance=±5% resistance=220 package=THT]
  R4 = Resistor [tolerance=±5% resistance=220 package=THT]
  元件2 = Arduino Uno (Rev3)
  S1 = Pushbutton [package="[THT]"]
  R5 = Resistor [tolerance=±5% resistance=10k package=THT]
  C1 = Ceramic Capacitor [capacitance=100nF package="100 mil [THT, multilayer]"]

nets:
  N1: IC1.In_1, U1.Pin_5, R2.Pin_1
  N2: IC1.Out_1_(_Controlled_by_Enable_1_), M1.pin_2, D1.anode, D2.cathode
  N3: IC1.0V, D2.anode, D4.anode, U1.Pin_4, U2.Pin_4, 元件2.GND, R5.Pin_1, C1.1
  N4: IC1.Out_2_(_Controlled_by_Enable_1_), M1.pin_1, D3.anode, D4.cathode
  N5: IC1.In_2, U2.Pin_5, R1.Pin_1
  N6: IC1.+Vmotor, IC1.+V, D1.cathode, D3.cathode
  N7: U1.Pin_1, R3.Pin_1
  N8: U1.Pin_2, 元件2.D10_PWM/SS
  N9: U2.Pin_1, R4.Pin_1
  N10: U2.Pin_2, 元件2.D9_PWM
  N11: R1.Pin_0, R4.Pin_0, S1.Pin_3, S1.Pin_4
  N12: R2.Pin_0, R3.Pin_0, 元件2.3V3
  N13: 元件2.D2, S1.Pin_1, S1.Pin_2, R5.Pin_0, C1.0
